// Logisim project RiscV.circ as structural Verilog: 15 circuits, main circuit main
module main (
  output [31:0] out_1,
  output [31:0] out_2
);

  wire alu_1_zero, and_1_out, CLK, control_1_aluop0, control_1_aluop1, control_1_alusrc, control_1_branch,
       control_1_memread, control_1_memtoreg, control_1_memwrite, control_1_regwrite, extomem_1_branchout,
       extomem_1_memreadout, extomem_1_memtoregout, extomem_1_memwriteout, extomem_1_regwriteout,
       extomem_1_zeroout, idtoex_1_alusrcout, idtoex_1_branchout, idtoex_1_memreadout, idtoex_1_memtoregout,
       idtoex_1_memwriteout, idtoex_1_regwriteout, memtowb_1_memtoregout, memtowb_1_regwriteout;
  wire [1:0] iftoid_1_instout_6;
  wire [3:0] alu_control_1_out_3;
  wire [4:0] extomem_1_writergout, idtoex_1_writergout, iftoid_1_instout_3, iftoid_1_instout_4,
       iftoid_1_instout_5, memtowb_1_writergout;
  wire [5:2] iftoid_1_instout_7;
  wire [6:0] iftoid_1_instout_2;
  wire [7:0] extomem_1_aluout;
  wire [31:0] adder_2_out, alu_1_out_5, banco_de_registradores_1_readdata1,
       banco_de_registradores_1_readdata2, data_memory_1_readdata, extomem_1_pcout, extomem_1_rd2out,
       idtoex_1_immout, idtoex_1_pcout, idtoex_1_rd1out, idtoex_1_rd2out, iftoid_1_pcout, immgen_1_s1,
       instruction_memory_1_instruction, memtowb_1_aluout, memtowb_1_rdout, multiplexer_1_out,
       multiplexer_2_out, multiplexer_3_out;
  wire [31:8] extomem_1_aluout_2;
  wire [31:25] iftoid_1_instout;

  Multiplexer #(.width(32)) multiplexer_1 (
    .in0(out_2), .in1(extomem_1_pcout), .out(multiplexer_1_out), .sel(and_1_out));
  PC pc_1 (.CLK(CLK), .in_2(multiplexer_1_out), .out_3(out_1));
  Adder #(.width(32)) adder_1 (.a(out_1), .b(32'h4), .out(out_2));  // open: cin, cout
  Instruction_Memory instruction_memory_1 (.ReadAdress(out_1[7:0]), .Instruction(instruction_memory_1_instruction));
  // Probe on instruction_memory_1_instruction
  IFtoID iftoid_1 (
    .CLK(CLK), .PCin(out_1), .INSTin(instruction_memory_1_instruction), .PCout(iftoid_1_pcout),
    .INSTout({iftoid_1_instout[31], iftoid_1_instout_7[3], iftoid_1_instout[29:25], iftoid_1_instout_4, iftoid_1_instout_3, iftoid_1_instout_7[2], iftoid_1_instout_6, iftoid_1_instout_5, iftoid_1_instout_2}));
  // Probe on {iftoid_1_instout[31], iftoid_1_instout_7[3], iftoid_1_instout[29:25], iftoid_1_instout_4, iftoid_1_instout_3, iftoid_1_instout_7[2], iftoid_1_instout_6, iftoid_1_instout_5, iftoid_1_instout_2}
  // Probe on iftoid_1_instout_2
  // Probe on iftoid_1_instout_5
  // Probe on iftoid_1_instout_3
  // Probe on iftoid_1_instout_4
  // Probe on memtowb_1_writergout
  // Probe on multiplexer_3_out
  Control control_1 (
    .opcode(iftoid_1_instout_2), .funct3(iftoid_1_instout_6), .AluSrc(control_1_alusrc),
    .MemToReg(control_1_memtoreg), .RegWrite(control_1_regwrite), .MemRead(control_1_memread),
    .MemWrite(control_1_memwrite), .Branch(control_1_branch), .AluOp0(control_1_aluop0),
    .AluOp1(control_1_aluop1));
  Banco_de_Registradores banco_de_registradores_1 (
    .CLK(CLK), .ReadRegister1(iftoid_1_instout_3), .ReadRegister2(iftoid_1_instout_4),
    .WriteRegister(memtowb_1_writergout), .RegWrite(memtowb_1_regwriteout), .WriteData(multiplexer_3_out),
    .ReadData1(banco_de_registradores_1_readdata1), .ReadData2(banco_de_registradores_1_readdata2));
  ImmGen immgen_1 (
    .in_1({iftoid_1_instout[31], iftoid_1_instout_7[3], iftoid_1_instout[29:25], iftoid_1_instout_4, iftoid_1_instout_3, iftoid_1_instout_7[2], iftoid_1_instout_6, iftoid_1_instout_5, iftoid_1_instout_2}),
    .S1(immgen_1_s1));
  Clock clock_1 (.out(CLK));
  IDtoEX idtoex_1 (
    .CLK(CLK), .ALUSRCin(control_1_alusrc), .MEMTOREGin(control_1_memtoreg), .REGWRITEin(control_1_regwrite),
    .MEMREADin(control_1_memread), .MEMWRITEin(control_1_memwrite), .BRANCHin(control_1_branch),
    .ALUOP0in(control_1_aluop0), .ALUOP1in(control_1_aluop1), .PCin(iftoid_1_pcout),
    .RD1in(banco_de_registradores_1_readdata1), .RD2in(banco_de_registradores_1_readdata2),
    .IMMin(immgen_1_s1), .WRITERGin(iftoid_1_instout_5), .ALUSRCout(idtoex_1_alusrcout),
    .MEMTOREGout(idtoex_1_memtoregout), .REGWRITEout(idtoex_1_regwriteout), .MEMREADout(idtoex_1_memreadout),
    .MEMWRITEout(idtoex_1_memwriteout), .BRANCHout(idtoex_1_branchout), .ALUOP0out(iftoid_1_instout_7[4]),
    .ALUOP1out(iftoid_1_instout_7[5]), .PCout(idtoex_1_pcout), .RD1out(idtoex_1_rd1out),
    .RD2out(idtoex_1_rd2out), .IMMout(idtoex_1_immout), .WRITERGout(idtoex_1_writergout));
  // Probe on idtoex_1_rd1out
  // Probe on idtoex_1_rd2out
  // Probe on idtoex_1_immout
  Multiplexer #(.width(32)) multiplexer_2 (
    .in0(idtoex_1_rd2out), .in1(idtoex_1_immout), .out(multiplexer_2_out), .sel(idtoex_1_alusrcout));
  ALU_Control alu_control_1 (
    .in_1({iftoid_1_instout_7, iftoid_1_instout_6}), .out_3(alu_control_1_out_3));  // open: in_2, out_4
  Adder #(.width(32)) adder_2 (.a(idtoex_1_pcout), .b(idtoex_1_immout), .out(adder_2_out));  // open: cin, cout
  ALU alu_1 (
    .in_1(idtoex_1_rd1out), .in_2(multiplexer_2_out), .ALUOp(alu_control_1_out_3), .Zero(alu_1_zero),
    .out_5(alu_1_out_5));
  // Probe on alu_1_out_5
  EXtoMEM extomem_1 (
    .CLK(CLK), .MEMTOREGin(idtoex_1_memtoregout), .REGWRITEin(idtoex_1_regwriteout),
    .MEMREADin(idtoex_1_memreadout), .MEMWRITEin(idtoex_1_memwriteout), .BRANCHin(idtoex_1_branchout),
    .PCin(adder_2_out), .ZEROin(alu_1_zero), .ALUin(alu_1_out_5), .RD2in(idtoex_1_rd2out),
    .WRITERGin(idtoex_1_writergout), .MEMTOREGout(extomem_1_memtoregout),
    .REGWRITEout(extomem_1_regwriteout), .MEMREADout(extomem_1_memreadout),
    .MEMWRITEout(extomem_1_memwriteout), .BRANCHout(extomem_1_branchout), .PCout(extomem_1_pcout),
    .ZEROout(extomem_1_zeroout), .ALUout({extomem_1_aluout_2, extomem_1_aluout}), .RD2out(extomem_1_rd2out),
    .WRITERGout(extomem_1_writergout));
  and and_1 (and_1_out, extomem_1_branchout, extomem_1_zeroout);
  Data_Memory data_memory_1 (
    .Adress(extomem_1_aluout), .MemWrite(extomem_1_memwriteout), .MemRead(extomem_1_memreadout), .CLK(CLK),
    .WriteData(extomem_1_rd2out), .ReadData(data_memory_1_readdata));
  MEMtoWB memtowb_1 (
    .CLK(CLK), .MEMTOREGin(extomem_1_memtoregout), .REGWRITEin(extomem_1_regwriteout),
    .RDin(data_memory_1_readdata), .ALUin({extomem_1_aluout_2, extomem_1_aluout}),
    .WRITERGin(extomem_1_writergout), .MEMTOREGout(memtowb_1_memtoregout),
    .REGWRITEout(memtowb_1_regwriteout), .RDout(memtowb_1_rdout), .ALUout(memtowb_1_aluout),
    .WRITERGout(memtowb_1_writergout));
  Multiplexer #(.width(32)) multiplexer_3 (
    .in0(memtowb_1_rdout), .in1(memtowb_1_aluout), .out(multiplexer_3_out), .sel(memtowb_1_memtoregout));
endmodule

module Registrador_32bits (
  input  CLK,
  input  [31:0] in_2,
  output bit_0,
  output bit_1,
  output bit_2,
  output bit_3,
  output bit_4,
  output bit_5,
  output bit_6,
  output bit_7,
  output bit_8,
  output bit_9,
  output bit_10,
  output bit_11,
  output bit_12,
  output bit_13,
  output bit_14,
  output bit_15,
  output bit_16,
  output bit_17,
  output bit_18,
  output bit_19,
  output bit_20,
  output bit_21,
  output bit_22,
  output bit_23,
  output bit_24,
  output bit_25,
  output bit_26,
  output bit_27,
  output bit_28,
  output bit_29,
  output bit_30,
  output bit_31
);

  wire d_ff_1_qn, d_ff_2_qn, d_ff_3_qn, d_ff_4_qn, d_ff_5_qn, d_ff_6_qn, d_ff_7_qn, d_ff_8_qn, d_ff_9_qn,
       d_ff_10_qn, d_ff_11_qn, d_ff_12_qn, d_ff_13_qn, d_ff_14_qn, d_ff_15_qn, d_ff_16_qn, d_ff_17_qn,
       d_ff_18_qn, d_ff_19_qn, d_ff_20_qn, d_ff_21_qn, d_ff_22_qn, d_ff_23_qn, d_ff_24_qn, d_ff_25_qn,
       d_ff_26_qn, d_ff_27_qn, d_ff_28_qn, d_ff_29_qn, d_ff_30_qn, d_ff_31_qn, d_ff_32_qn, undriven,
       undriven_2, undriven_3, undriven_4, undriven_5, undriven_6;

  D_Flip_Flop d_ff_1 (.D(in_2[0]), .clk(CLK), .Q(bit_0), .Qn(d_ff_1_qn), .preset(undriven), .reset(undriven_2));
  D_Flip_Flop d_ff_2 (.D(in_2[8]), .clk(CLK), .Q(bit_8), .Qn(d_ff_2_qn), .preset(undriven_2), .reset(undriven_3));
  D_Flip_Flop d_ff_3 (.D(in_2[16]), .clk(CLK), .Q(bit_16), .Qn(d_ff_3_qn), .preset(undriven_3), .reset(undriven_4));
  D_Flip_Flop d_ff_4 (.D(in_2[24]), .clk(CLK), .Q(bit_24), .Qn(d_ff_4_qn), .preset(undriven_4), .reset(undriven_5));
  // NoConnect on d_ff_1_qn
  // NoConnect on d_ff_2_qn
  // NoConnect on d_ff_3_qn
  // NoConnect on d_ff_4_qn
  D_Flip_Flop d_ff_5 (.D(in_2[1]), .clk(CLK), .Q(bit_1), .Qn(d_ff_5_qn), .preset(undriven), .reset(undriven_2));
  D_Flip_Flop d_ff_6 (.D(in_2[9]), .clk(CLK), .Q(bit_9), .Qn(d_ff_6_qn), .preset(undriven_2), .reset(undriven_3));
  D_Flip_Flop d_ff_7 (.D(in_2[17]), .clk(CLK), .Q(bit_17), .Qn(d_ff_7_qn), .preset(undriven_3), .reset(undriven_4));
  D_Flip_Flop d_ff_8 (.D(in_2[25]), .clk(CLK), .Q(bit_25), .Qn(d_ff_8_qn), .preset(undriven_4), .reset(undriven_5));
  // NoConnect on d_ff_5_qn
  // NoConnect on d_ff_6_qn
  // NoConnect on d_ff_7_qn
  // NoConnect on d_ff_8_qn
  D_Flip_Flop d_ff_9 (.D(in_2[2]), .clk(CLK), .Q(bit_2), .Qn(d_ff_9_qn), .preset(undriven), .reset(undriven_2));
  D_Flip_Flop d_ff_10 (.D(in_2[10]), .clk(CLK), .Q(bit_10), .Qn(d_ff_10_qn), .preset(undriven_2), .reset(undriven_3));
  D_Flip_Flop d_ff_11 (.D(in_2[18]), .clk(CLK), .Q(bit_18), .Qn(d_ff_11_qn), .preset(undriven_3), .reset(undriven_4));
  D_Flip_Flop d_ff_12 (.D(in_2[26]), .clk(CLK), .Q(bit_26), .Qn(d_ff_12_qn), .preset(undriven_4), .reset(undriven_5));
  // NoConnect on d_ff_9_qn
  // NoConnect on d_ff_10_qn
  // NoConnect on d_ff_11_qn
  // NoConnect on d_ff_12_qn
  D_Flip_Flop d_ff_13 (.D(in_2[3]), .clk(CLK), .Q(bit_3), .Qn(d_ff_13_qn), .preset(undriven), .reset(undriven_2));
  D_Flip_Flop d_ff_14 (.D(in_2[11]), .clk(CLK), .Q(bit_11), .Qn(d_ff_14_qn), .preset(undriven_2), .reset(undriven_3));
  D_Flip_Flop d_ff_15 (.D(in_2[19]), .clk(CLK), .Q(bit_19), .Qn(d_ff_15_qn), .preset(undriven_3), .reset(undriven_4));
  D_Flip_Flop d_ff_16 (.D(in_2[27]), .clk(CLK), .Q(bit_27), .Qn(d_ff_16_qn), .preset(undriven_4), .reset(undriven_5));
  // NoConnect on d_ff_13_qn
  // NoConnect on d_ff_14_qn
  // NoConnect on d_ff_15_qn
  // NoConnect on d_ff_16_qn
  D_Flip_Flop d_ff_17 (.D(in_2[4]), .clk(CLK), .Q(bit_4), .Qn(d_ff_17_qn), .preset(undriven), .reset(undriven_2));
  D_Flip_Flop d_ff_18 (.D(in_2[12]), .clk(CLK), .Q(bit_12), .Qn(d_ff_18_qn), .preset(undriven_2), .reset(undriven_3));
  D_Flip_Flop d_ff_19 (.D(in_2[20]), .clk(CLK), .Q(bit_20), .Qn(d_ff_19_qn), .preset(undriven_3), .reset(undriven_4));
  D_Flip_Flop d_ff_20 (.D(in_2[28]), .clk(CLK), .Q(bit_28), .Qn(d_ff_20_qn), .preset(undriven_4), .reset(undriven_5));
  // NoConnect on d_ff_17_qn
  // NoConnect on d_ff_18_qn
  // NoConnect on d_ff_19_qn
  // NoConnect on d_ff_20_qn
  D_Flip_Flop d_ff_21 (.D(in_2[5]), .clk(CLK), .Q(bit_5), .Qn(d_ff_21_qn), .preset(undriven), .reset(undriven_2));
  D_Flip_Flop d_ff_22 (.D(in_2[13]), .clk(CLK), .Q(bit_13), .Qn(d_ff_22_qn), .preset(undriven_2), .reset(undriven_3));
  D_Flip_Flop d_ff_23 (.D(in_2[21]), .clk(CLK), .Q(bit_21), .Qn(d_ff_23_qn), .preset(undriven_3), .reset(undriven_4));
  D_Flip_Flop d_ff_24 (.D(in_2[29]), .clk(CLK), .Q(bit_29), .Qn(d_ff_24_qn), .preset(undriven_4), .reset(undriven_5));
  // NoConnect on d_ff_21_qn
  // NoConnect on d_ff_22_qn
  // NoConnect on d_ff_23_qn
  // NoConnect on d_ff_24_qn
  D_Flip_Flop d_ff_25 (.D(in_2[6]), .clk(CLK), .Q(bit_6), .Qn(d_ff_25_qn), .preset(undriven), .reset(undriven_2));
  D_Flip_Flop d_ff_26 (.D(in_2[14]), .clk(CLK), .Q(bit_14), .Qn(d_ff_26_qn), .preset(undriven_2), .reset(undriven_3));
  D_Flip_Flop d_ff_27 (.D(in_2[22]), .clk(CLK), .Q(bit_22), .Qn(d_ff_27_qn), .preset(undriven_3), .reset(undriven_4));
  D_Flip_Flop d_ff_28 (.D(in_2[30]), .clk(CLK), .Q(bit_30), .Qn(d_ff_28_qn), .preset(undriven_4), .reset(undriven_5));
  // NoConnect on d_ff_25_qn
  // NoConnect on d_ff_26_qn
  // NoConnect on d_ff_27_qn
  // NoConnect on d_ff_28_qn
  D_Flip_Flop d_ff_29 (.D(in_2[7]), .clk(CLK), .Q(bit_7), .Qn(d_ff_29_qn), .preset(undriven), .reset(undriven_2));
  D_Flip_Flop d_ff_30 (.D(in_2[15]), .clk(CLK), .Q(bit_15), .Qn(d_ff_30_qn), .preset(undriven_2), .reset(undriven_3));
  D_Flip_Flop d_ff_31 (.D(in_2[23]), .clk(CLK), .Q(bit_23), .Qn(d_ff_31_qn), .preset(undriven_3), .reset(undriven_4));
  D_Flip_Flop d_ff_32 (.D(in_2[31]), .clk(CLK), .Q(bit_31), .Qn(d_ff_32_qn), .preset(undriven_4), .reset(undriven_5));
  // NoConnect on undriven
  // NoConnect on d_ff_29_qn
  // NoConnect on d_ff_30_qn
  // NoConnect on d_ff_31_qn
  // NoConnect on d_ff_32_qn
  // NoConnect on undriven_2
  // NoConnect on undriven_3
  // NoConnect on undriven_4
  // NoConnect on undriven_6
  // NoConnect on undriven_5

  // Other names for the same wires on the sheet: bit_0_t = in_2[0]; bit_1_t = in_2[1]; bit_2_t = in_2[2];
  //   bit_3_t = in_2[3]; bit_4_t = in_2[4]; bit_5_t = in_2[5]; bit_6_t = in_2[6]; bit_7_t = in_2[7];
  //   bit_8_t = in_2[8]; bit_9_t = in_2[9]; bit_10_t = in_2[10]; bit_11_t = in_2[11]; bit_12_t = in_2[12];
  //   bit_13_t = in_2[13]; bit_14_t = in_2[14]; bit_15_t = in_2[15]; bit_16_t = in_2[16]; bit_17_t = in_2[17];
  //   bit_18_t = in_2[18]; bit_19_t = in_2[19]; bit_20_t = in_2[20]; bit_21_t = in_2[21]; bit_22_t = in_2[22];
  //   bit_23_t = in_2[23]; bit_24_t = in_2[24]; bit_25_t = in_2[25]; bit_26_t = in_2[26]; bit_27_t = in_2[27];
  //   bit_28_t = in_2[28]; bit_29_t = in_2[29]; bit_30_t = in_2[30]; bit_31_t = in_2[31]
endmodule

module Banco_de_Registradores (
  input  CLK,
  input  [4:0] ReadRegister1,
  input  [4:0] ReadRegister2,
  input  [4:0] WriteRegister,
  input  RegWrite,
  input  [31:0] WriteData,
  output [31:0] ReadData1,
  output [31:0] ReadData2
);

  wire [31:0] reg_1, reg_2, reg_3, reg_4, reg_5, reg_6, reg_7, reg_8, reg_9, reg_10, reg_11, reg_12, reg_13,
       reg_14, reg_15, reg_16, reg_17, reg_18, reg_19, reg_20, reg_21, reg_22, reg_23, reg_24, reg_25,
       reg_26, reg_27, reg_28, reg_29, reg_30, reg_31, reg_x0, reg_x1, reg_x2, reg_x3, reg_x4, reg_x5,
       reg_x6, reg_x7, reg_x8, reg_x9, reg_x10, reg_x11, reg_x12, reg_x13, reg_x14, reg_x15, reg_x16,
       reg_x17, reg_x18, reg_x19, reg_x20, reg_x21, reg_x22, reg_x23, reg_x24, reg_x25, reg_x26, reg_x27,
       reg_x28, reg_x29, reg_x30, reg_x31;

  Multiplexer #(.enable("true"), .select(5), .width(32)) multiplexer_1 (
    .in0({32{1'b0}}), .in1(reg_1), .in2(reg_2), .in3(reg_3), .in4(reg_4), .in5(reg_5), .in6(reg_6),
    .in7(reg_7), .in8(reg_8), .in9(reg_9), .in10(reg_10), .in11(reg_11), .in12(reg_12), .in13(reg_13),
    .in14(reg_14), .in15(reg_15), .in16(reg_16), .in17(reg_17), .in18(reg_18), .in19(reg_19), .in20(reg_20),
    .in21(reg_21), .in22(reg_22), .in23(reg_23), .in24(reg_24), .in25(reg_25), .in26(reg_26), .in27(reg_27),
    .in28(reg_28), .in29(reg_29), .in30(reg_30), .in31(reg_31), .out(ReadData1), .sel(ReadRegister1));  // open: en
  Multiplexer #(.enable("true"), .select(5), .width(32)) multiplexer_2 (
    .in0({32{1'b0}}), .in1(reg_1), .in2(reg_2), .in3(reg_3), .in4(reg_4), .in5(reg_5), .in6(reg_6),
    .in7(reg_7), .in8(reg_8), .in9(reg_9), .in10(reg_10), .in11(reg_11), .in12(reg_12), .in13(reg_13),
    .in14(reg_14), .in15(reg_15), .in16(reg_16), .in17(reg_17), .in18(reg_18), .in19(reg_19), .in20(reg_20),
    .in21(reg_21), .in22(reg_22), .in23(reg_23), .in24(reg_24), .in25(reg_25), .in26(reg_26), .in27(reg_27),
    .in28(reg_28), .in29(reg_29), .in30(reg_30), .in31(reg_31), .out(ReadData2), .sel(ReadRegister2));  // open: en
  Demultiplexer #(.enable("true"), .select(5), .width(32)) demultiplexer_1 (
    .out0(reg_x0), .out1(reg_x1), .out2(reg_x2), .out3(reg_x3), .out4(reg_x4), .out5(reg_x5), .out6(reg_x6),
    .out7(reg_x7), .out8(reg_x8), .out9(reg_x9), .out10(reg_x10), .out11(reg_x11), .out12(reg_x12),
    .out13(reg_x13), .out14(reg_x14), .out15(reg_x15), .out16(reg_x16), .out17(reg_x17), .out18(reg_x18),
    .out19(reg_x19), .out20(reg_x20), .out21(reg_x21), .out22(reg_x22), .out23(reg_x23), .out24(reg_x24),
    .out25(reg_x25), .out26(reg_x26), .out27(reg_x27), .out28(reg_x28), .out29(reg_x29), .out30(reg_x30),
    .out31(reg_x31), .in(WriteData), .sel(WriteRegister), .en(RegWrite));
  Registrador_32bits registrador_32bits_1 (
    .CLK(CLK), .in_2(reg_x1), .bit_0(reg_1[0]), .bit_1(reg_1[1]), .bit_2(reg_1[2]), .bit_3(reg_1[3]),
    .bit_4(reg_1[4]), .bit_5(reg_1[5]), .bit_6(reg_1[6]), .bit_7(reg_1[7]), .bit_8(reg_1[8]),
    .bit_9(reg_1[9]), .bit_10(reg_1[10]), .bit_11(reg_1[11]), .bit_12(reg_1[12]), .bit_13(reg_1[13]),
    .bit_14(reg_1[14]), .bit_15(reg_1[15]), .bit_16(reg_1[16]), .bit_17(reg_1[17]), .bit_18(reg_1[18]),
    .bit_19(reg_1[19]), .bit_20(reg_1[20]), .bit_21(reg_1[21]), .bit_22(reg_1[22]), .bit_23(reg_1[23]),
    .bit_24(reg_1[24]), .bit_25(reg_1[25]), .bit_26(reg_1[26]), .bit_27(reg_1[27]), .bit_28(reg_1[28]),
    .bit_29(reg_1[29]), .bit_30(reg_1[30]), .bit_31(reg_1[31]));
  Registrador_32bits registrador_32bits_2 (
    .CLK(CLK), .in_2(reg_x5), .bit_0(reg_5[0]), .bit_1(reg_5[1]), .bit_2(reg_5[2]), .bit_3(reg_5[3]),
    .bit_4(reg_5[4]), .bit_5(reg_5[5]), .bit_6(reg_5[6]), .bit_7(reg_5[7]), .bit_8(reg_5[8]),
    .bit_9(reg_5[9]), .bit_10(reg_5[10]), .bit_11(reg_5[11]), .bit_12(reg_5[12]), .bit_13(reg_5[13]),
    .bit_14(reg_5[14]), .bit_15(reg_5[15]), .bit_16(reg_5[16]), .bit_17(reg_5[17]), .bit_18(reg_5[18]),
    .bit_19(reg_5[19]), .bit_20(reg_5[20]), .bit_21(reg_5[21]), .bit_22(reg_5[22]), .bit_23(reg_5[23]),
    .bit_24(reg_5[24]), .bit_25(reg_5[25]), .bit_26(reg_5[26]), .bit_27(reg_5[27]), .bit_28(reg_5[28]),
    .bit_29(reg_5[29]), .bit_30(reg_5[30]), .bit_31(reg_5[31]));
  Registrador_32bits registrador_32bits_3 (
    .CLK(CLK), .in_2(reg_x9), .bit_0(reg_9[0]), .bit_1(reg_9[1]), .bit_2(reg_9[2]), .bit_3(reg_9[3]),
    .bit_4(reg_9[4]), .bit_5(reg_9[5]), .bit_6(reg_9[6]), .bit_7(reg_9[7]), .bit_8(reg_9[8]),
    .bit_9(reg_9[9]), .bit_10(reg_9[10]), .bit_11(reg_9[11]), .bit_12(reg_9[12]), .bit_13(reg_9[13]),
    .bit_14(reg_9[14]), .bit_15(reg_9[15]), .bit_16(reg_9[16]), .bit_17(reg_9[17]), .bit_18(reg_9[18]),
    .bit_19(reg_9[19]), .bit_20(reg_9[20]), .bit_21(reg_9[21]), .bit_22(reg_9[22]), .bit_23(reg_9[23]),
    .bit_24(reg_9[24]), .bit_25(reg_9[25]), .bit_26(reg_9[26]), .bit_27(reg_9[27]), .bit_28(reg_9[28]),
    .bit_29(reg_9[29]), .bit_30(reg_9[30]), .bit_31(reg_9[31]));
  Registrador_32bits registrador_32bits_4 (
    .CLK(CLK), .in_2(reg_x13), .bit_0(reg_13[0]), .bit_1(reg_13[1]), .bit_2(reg_13[2]), .bit_3(reg_13[3]),
    .bit_4(reg_13[4]), .bit_5(reg_13[5]), .bit_6(reg_13[6]), .bit_7(reg_13[7]), .bit_8(reg_13[8]),
    .bit_9(reg_13[9]), .bit_10(reg_13[10]), .bit_11(reg_13[11]), .bit_12(reg_13[12]), .bit_13(reg_13[13]),
    .bit_14(reg_13[14]), .bit_15(reg_13[15]), .bit_16(reg_13[16]), .bit_17(reg_13[17]), .bit_18(reg_13[18]),
    .bit_19(reg_13[19]), .bit_20(reg_13[20]), .bit_21(reg_13[21]), .bit_22(reg_13[22]), .bit_23(reg_13[23]),
    .bit_24(reg_13[24]), .bit_25(reg_13[25]), .bit_26(reg_13[26]), .bit_27(reg_13[27]), .bit_28(reg_13[28]),
    .bit_29(reg_13[29]), .bit_30(reg_13[30]), .bit_31(reg_13[31]));
  Registrador_32bits registrador_32bits_5 (
    .CLK(CLK), .in_2(reg_x17), .bit_0(reg_17[0]), .bit_1(reg_17[1]), .bit_2(reg_17[2]), .bit_3(reg_17[3]),
    .bit_4(reg_17[4]), .bit_5(reg_17[5]), .bit_6(reg_17[6]), .bit_7(reg_17[7]), .bit_8(reg_17[8]),
    .bit_9(reg_17[9]), .bit_10(reg_17[10]), .bit_11(reg_17[11]), .bit_12(reg_17[12]), .bit_13(reg_17[13]),
    .bit_14(reg_17[14]), .bit_15(reg_17[15]), .bit_16(reg_17[16]), .bit_17(reg_17[17]), .bit_18(reg_17[18]),
    .bit_19(reg_17[19]), .bit_20(reg_17[20]), .bit_21(reg_17[21]), .bit_22(reg_17[22]), .bit_23(reg_17[23]),
    .bit_24(reg_17[24]), .bit_25(reg_17[25]), .bit_26(reg_17[26]), .bit_27(reg_17[27]), .bit_28(reg_17[28]),
    .bit_29(reg_17[29]), .bit_30(reg_17[30]), .bit_31(reg_17[31]));
  Registrador_32bits registrador_32bits_6 (
    .CLK(CLK), .in_2(reg_x21), .bit_0(reg_21[0]), .bit_1(reg_21[1]), .bit_2(reg_21[2]), .bit_3(reg_21[3]),
    .bit_4(reg_21[4]), .bit_5(reg_21[5]), .bit_6(reg_21[6]), .bit_7(reg_21[7]), .bit_8(reg_21[8]),
    .bit_9(reg_21[9]), .bit_10(reg_21[10]), .bit_11(reg_21[11]), .bit_12(reg_21[12]), .bit_13(reg_21[13]),
    .bit_14(reg_21[14]), .bit_15(reg_21[15]), .bit_16(reg_21[16]), .bit_17(reg_21[17]), .bit_18(reg_21[18]),
    .bit_19(reg_21[19]), .bit_20(reg_21[20]), .bit_21(reg_21[21]), .bit_22(reg_21[22]), .bit_23(reg_21[23]),
    .bit_24(reg_21[24]), .bit_25(reg_21[25]), .bit_26(reg_21[26]), .bit_27(reg_21[27]), .bit_28(reg_21[28]),
    .bit_29(reg_21[29]), .bit_30(reg_21[30]), .bit_31(reg_21[31]));
  Registrador_32bits registrador_32bits_7 (
    .CLK(CLK), .in_2(reg_x25), .bit_0(reg_25[0]), .bit_1(reg_25[1]), .bit_2(reg_25[2]), .bit_3(reg_25[3]),
    .bit_4(reg_25[4]), .bit_5(reg_25[5]), .bit_6(reg_25[6]), .bit_7(reg_25[7]), .bit_8(reg_25[8]),
    .bit_9(reg_25[9]), .bit_10(reg_25[10]), .bit_11(reg_25[11]), .bit_12(reg_25[12]), .bit_13(reg_25[13]),
    .bit_14(reg_25[14]), .bit_15(reg_25[15]), .bit_16(reg_25[16]), .bit_17(reg_25[17]), .bit_18(reg_25[18]),
    .bit_19(reg_25[19]), .bit_20(reg_25[20]), .bit_21(reg_25[21]), .bit_22(reg_25[22]), .bit_23(reg_25[23]),
    .bit_24(reg_25[24]), .bit_25(reg_25[25]), .bit_26(reg_25[26]), .bit_27(reg_25[27]), .bit_28(reg_25[28]),
    .bit_29(reg_25[29]), .bit_30(reg_25[30]), .bit_31(reg_25[31]));
  Registrador_32bits registrador_32bits_8 (
    .CLK(CLK), .in_2(reg_x29), .bit_0(reg_29[0]), .bit_1(reg_29[1]), .bit_2(reg_29[2]), .bit_3(reg_29[3]),
    .bit_4(reg_29[4]), .bit_5(reg_29[5]), .bit_6(reg_29[6]), .bit_7(reg_29[7]), .bit_8(reg_29[8]),
    .bit_9(reg_29[9]), .bit_10(reg_29[10]), .bit_11(reg_29[11]), .bit_12(reg_29[12]), .bit_13(reg_29[13]),
    .bit_14(reg_29[14]), .bit_15(reg_29[15]), .bit_16(reg_29[16]), .bit_17(reg_29[17]), .bit_18(reg_29[18]),
    .bit_19(reg_29[19]), .bit_20(reg_29[20]), .bit_21(reg_29[21]), .bit_22(reg_29[22]), .bit_23(reg_29[23]),
    .bit_24(reg_29[24]), .bit_25(reg_29[25]), .bit_26(reg_29[26]), .bit_27(reg_29[27]), .bit_28(reg_29[28]),
    .bit_29(reg_29[29]), .bit_30(reg_29[30]), .bit_31(reg_29[31]));
  Registrador_32bits registrador_32bits_9 (
    .CLK(CLK), .in_2(reg_x2), .bit_0(reg_2[0]), .bit_1(reg_2[1]), .bit_2(reg_2[2]), .bit_3(reg_2[3]),
    .bit_4(reg_2[4]), .bit_5(reg_2[5]), .bit_6(reg_2[6]), .bit_7(reg_2[7]), .bit_8(reg_2[8]),
    .bit_9(reg_2[9]), .bit_10(reg_2[10]), .bit_11(reg_2[11]), .bit_12(reg_2[12]), .bit_13(reg_2[13]),
    .bit_14(reg_2[14]), .bit_15(reg_2[15]), .bit_16(reg_2[16]), .bit_17(reg_2[17]), .bit_18(reg_2[18]),
    .bit_19(reg_2[19]), .bit_20(reg_2[20]), .bit_21(reg_2[21]), .bit_22(reg_2[22]), .bit_23(reg_2[23]),
    .bit_24(reg_2[24]), .bit_25(reg_2[25]), .bit_26(reg_2[26]), .bit_27(reg_2[27]), .bit_28(reg_2[28]),
    .bit_29(reg_2[29]), .bit_30(reg_2[30]), .bit_31(reg_2[31]));
  Registrador_32bits registrador_32bits_10 (
    .CLK(CLK), .in_2(reg_x6), .bit_0(reg_6[0]), .bit_1(reg_6[1]), .bit_2(reg_6[2]), .bit_3(reg_6[3]),
    .bit_4(reg_6[4]), .bit_5(reg_6[5]), .bit_6(reg_6[6]), .bit_7(reg_6[7]), .bit_8(reg_6[8]),
    .bit_9(reg_6[9]), .bit_10(reg_6[10]), .bit_11(reg_6[11]), .bit_12(reg_6[12]), .bit_13(reg_6[13]),
    .bit_14(reg_6[14]), .bit_15(reg_6[15]), .bit_16(reg_6[16]), .bit_17(reg_6[17]), .bit_18(reg_6[18]),
    .bit_19(reg_6[19]), .bit_20(reg_6[20]), .bit_21(reg_6[21]), .bit_22(reg_6[22]), .bit_23(reg_6[23]),
    .bit_24(reg_6[24]), .bit_25(reg_6[25]), .bit_26(reg_6[26]), .bit_27(reg_6[27]), .bit_28(reg_6[28]),
    .bit_29(reg_6[29]), .bit_30(reg_6[30]), .bit_31(reg_6[31]));
  Registrador_32bits registrador_32bits_11 (
    .CLK(CLK), .in_2(reg_x10), .bit_0(reg_10[0]), .bit_1(reg_10[1]), .bit_2(reg_10[2]), .bit_3(reg_10[3]),
    .bit_4(reg_10[4]), .bit_5(reg_10[5]), .bit_6(reg_10[6]), .bit_7(reg_10[7]), .bit_8(reg_10[8]),
    .bit_9(reg_10[9]), .bit_10(reg_10[10]), .bit_11(reg_10[11]), .bit_12(reg_10[12]), .bit_13(reg_10[13]),
    .bit_14(reg_10[14]), .bit_15(reg_10[15]), .bit_16(reg_10[16]), .bit_17(reg_10[17]), .bit_18(reg_10[18]),
    .bit_19(reg_10[19]), .bit_20(reg_10[20]), .bit_21(reg_10[21]), .bit_22(reg_10[22]), .bit_23(reg_10[23]),
    .bit_24(reg_10[24]), .bit_25(reg_10[25]), .bit_26(reg_10[26]), .bit_27(reg_10[27]), .bit_28(reg_10[28]),
    .bit_29(reg_10[29]), .bit_30(reg_10[30]), .bit_31(reg_10[31]));
  Registrador_32bits registrador_32bits_12 (
    .CLK(CLK), .in_2(reg_x14), .bit_0(reg_14[0]), .bit_1(reg_14[1]), .bit_2(reg_14[2]), .bit_3(reg_14[3]),
    .bit_4(reg_14[4]), .bit_5(reg_14[5]), .bit_6(reg_14[6]), .bit_7(reg_14[7]), .bit_8(reg_14[8]),
    .bit_9(reg_14[9]), .bit_10(reg_14[10]), .bit_11(reg_14[11]), .bit_12(reg_14[12]), .bit_13(reg_14[13]),
    .bit_14(reg_14[14]), .bit_15(reg_14[15]), .bit_16(reg_14[16]), .bit_17(reg_14[17]), .bit_18(reg_14[18]),
    .bit_19(reg_14[19]), .bit_20(reg_14[20]), .bit_21(reg_14[21]), .bit_22(reg_14[22]), .bit_23(reg_14[23]),
    .bit_24(reg_14[24]), .bit_25(reg_14[25]), .bit_26(reg_14[26]), .bit_27(reg_14[27]), .bit_28(reg_14[28]),
    .bit_29(reg_14[29]), .bit_30(reg_14[30]), .bit_31(reg_14[31]));
  Registrador_32bits registrador_32bits_13 (
    .CLK(CLK), .in_2(reg_x18), .bit_0(reg_18[0]), .bit_1(reg_18[1]), .bit_2(reg_18[2]), .bit_3(reg_18[3]),
    .bit_4(reg_18[4]), .bit_5(reg_18[5]), .bit_6(reg_18[6]), .bit_7(reg_18[7]), .bit_8(reg_18[8]),
    .bit_9(reg_18[9]), .bit_10(reg_18[10]), .bit_11(reg_18[11]), .bit_12(reg_18[12]), .bit_13(reg_18[13]),
    .bit_14(reg_18[14]), .bit_15(reg_18[15]), .bit_16(reg_18[16]), .bit_17(reg_18[17]), .bit_18(reg_18[18]),
    .bit_19(reg_18[19]), .bit_20(reg_18[20]), .bit_21(reg_18[21]), .bit_22(reg_18[22]), .bit_23(reg_18[23]),
    .bit_24(reg_18[24]), .bit_25(reg_18[25]), .bit_26(reg_18[26]), .bit_27(reg_18[27]), .bit_28(reg_18[28]),
    .bit_29(reg_18[29]), .bit_30(reg_18[30]), .bit_31(reg_18[31]));
  Registrador_32bits registrador_32bits_14 (
    .CLK(CLK), .in_2(reg_x22), .bit_0(reg_22[0]), .bit_1(reg_22[1]), .bit_2(reg_22[2]), .bit_3(reg_22[3]),
    .bit_4(reg_22[4]), .bit_5(reg_22[5]), .bit_6(reg_22[6]), .bit_7(reg_22[7]), .bit_8(reg_22[8]),
    .bit_9(reg_22[9]), .bit_10(reg_22[10]), .bit_11(reg_22[11]), .bit_12(reg_22[12]), .bit_13(reg_22[13]),
    .bit_14(reg_22[14]), .bit_15(reg_22[15]), .bit_16(reg_22[16]), .bit_17(reg_22[17]), .bit_18(reg_22[18]),
    .bit_19(reg_22[19]), .bit_20(reg_22[20]), .bit_21(reg_22[21]), .bit_22(reg_22[22]), .bit_23(reg_22[23]),
    .bit_24(reg_22[24]), .bit_25(reg_22[25]), .bit_26(reg_22[26]), .bit_27(reg_22[27]), .bit_28(reg_22[28]),
    .bit_29(reg_22[29]), .bit_30(reg_22[30]), .bit_31(reg_22[31]));
  Registrador_32bits registrador_32bits_15 (
    .CLK(CLK), .in_2(reg_x26), .bit_0(reg_26[0]), .bit_1(reg_26[1]), .bit_2(reg_26[2]), .bit_3(reg_26[3]),
    .bit_4(reg_26[4]), .bit_5(reg_26[5]), .bit_6(reg_26[6]), .bit_7(reg_26[7]), .bit_8(reg_26[8]),
    .bit_9(reg_26[9]), .bit_10(reg_26[10]), .bit_11(reg_26[11]), .bit_12(reg_26[12]), .bit_13(reg_26[13]),
    .bit_14(reg_26[14]), .bit_15(reg_26[15]), .bit_16(reg_26[16]), .bit_17(reg_26[17]), .bit_18(reg_26[18]),
    .bit_19(reg_26[19]), .bit_20(reg_26[20]), .bit_21(reg_26[21]), .bit_22(reg_26[22]), .bit_23(reg_26[23]),
    .bit_24(reg_26[24]), .bit_25(reg_26[25]), .bit_26(reg_26[26]), .bit_27(reg_26[27]), .bit_28(reg_26[28]),
    .bit_29(reg_26[29]), .bit_30(reg_26[30]), .bit_31(reg_26[31]));
  Registrador_32bits registrador_32bits_16 (
    .CLK(CLK), .in_2(reg_x30), .bit_0(reg_30[0]), .bit_1(reg_30[1]), .bit_2(reg_30[2]), .bit_3(reg_30[3]),
    .bit_4(reg_30[4]), .bit_5(reg_30[5]), .bit_6(reg_30[6]), .bit_7(reg_30[7]), .bit_8(reg_30[8]),
    .bit_9(reg_30[9]), .bit_10(reg_30[10]), .bit_11(reg_30[11]), .bit_12(reg_30[12]), .bit_13(reg_30[13]),
    .bit_14(reg_30[14]), .bit_15(reg_30[15]), .bit_16(reg_30[16]), .bit_17(reg_30[17]), .bit_18(reg_30[18]),
    .bit_19(reg_30[19]), .bit_20(reg_30[20]), .bit_21(reg_30[21]), .bit_22(reg_30[22]), .bit_23(reg_30[23]),
    .bit_24(reg_30[24]), .bit_25(reg_30[25]), .bit_26(reg_30[26]), .bit_27(reg_30[27]), .bit_28(reg_30[28]),
    .bit_29(reg_30[29]), .bit_30(reg_30[30]), .bit_31(reg_30[31]));
  Registrador_32bits registrador_32bits_17 (
    .CLK(CLK), .in_2(reg_x3), .bit_0(reg_3[0]), .bit_1(reg_3[1]), .bit_2(reg_3[2]), .bit_3(reg_3[3]),
    .bit_4(reg_3[4]), .bit_5(reg_3[5]), .bit_6(reg_3[6]), .bit_7(reg_3[7]), .bit_8(reg_3[8]),
    .bit_9(reg_3[9]), .bit_10(reg_3[10]), .bit_11(reg_3[11]), .bit_12(reg_3[12]), .bit_13(reg_3[13]),
    .bit_14(reg_3[14]), .bit_15(reg_3[15]), .bit_16(reg_3[16]), .bit_17(reg_3[17]), .bit_18(reg_3[18]),
    .bit_19(reg_3[19]), .bit_20(reg_3[20]), .bit_21(reg_3[21]), .bit_22(reg_3[22]), .bit_23(reg_3[23]),
    .bit_24(reg_3[24]), .bit_25(reg_3[25]), .bit_26(reg_3[26]), .bit_27(reg_3[27]), .bit_28(reg_3[28]),
    .bit_29(reg_3[29]), .bit_30(reg_3[30]), .bit_31(reg_3[31]));
  Registrador_32bits registrador_32bits_18 (
    .CLK(CLK), .in_2(reg_x7), .bit_0(reg_7[0]), .bit_1(reg_7[1]), .bit_2(reg_7[2]), .bit_3(reg_7[3]),
    .bit_4(reg_7[4]), .bit_5(reg_7[5]), .bit_6(reg_7[6]), .bit_7(reg_7[7]), .bit_8(reg_7[8]),
    .bit_9(reg_7[9]), .bit_10(reg_7[10]), .bit_11(reg_7[11]), .bit_12(reg_7[12]), .bit_13(reg_7[13]),
    .bit_14(reg_7[14]), .bit_15(reg_7[15]), .bit_16(reg_7[16]), .bit_17(reg_7[17]), .bit_18(reg_7[18]),
    .bit_19(reg_7[19]), .bit_20(reg_7[20]), .bit_21(reg_7[21]), .bit_22(reg_7[22]), .bit_23(reg_7[23]),
    .bit_24(reg_7[24]), .bit_25(reg_7[25]), .bit_26(reg_7[26]), .bit_27(reg_7[27]), .bit_28(reg_7[28]),
    .bit_29(reg_7[29]), .bit_30(reg_7[30]), .bit_31(reg_7[31]));
  Registrador_32bits registrador_32bits_19 (
    .CLK(CLK), .in_2(reg_x11), .bit_0(reg_11[0]), .bit_1(reg_11[1]), .bit_2(reg_11[2]), .bit_3(reg_11[3]),
    .bit_4(reg_11[4]), .bit_5(reg_11[5]), .bit_6(reg_11[6]), .bit_7(reg_11[7]), .bit_8(reg_11[8]),
    .bit_9(reg_11[9]), .bit_10(reg_11[10]), .bit_11(reg_11[11]), .bit_12(reg_11[12]), .bit_13(reg_11[13]),
    .bit_14(reg_11[14]), .bit_15(reg_11[15]), .bit_16(reg_11[16]), .bit_17(reg_11[17]), .bit_18(reg_11[18]),
    .bit_19(reg_11[19]), .bit_20(reg_11[20]), .bit_21(reg_11[21]), .bit_22(reg_11[22]), .bit_23(reg_11[23]),
    .bit_24(reg_11[24]), .bit_25(reg_11[25]), .bit_26(reg_11[26]), .bit_27(reg_11[27]), .bit_28(reg_11[28]),
    .bit_29(reg_11[29]), .bit_30(reg_11[30]), .bit_31(reg_11[31]));
  Registrador_32bits registrador_32bits_20 (
    .CLK(CLK), .in_2(reg_x15), .bit_0(reg_15[0]), .bit_1(reg_15[1]), .bit_2(reg_15[2]), .bit_3(reg_15[3]),
    .bit_4(reg_15[4]), .bit_5(reg_15[5]), .bit_6(reg_15[6]), .bit_7(reg_15[7]), .bit_8(reg_15[8]),
    .bit_9(reg_15[9]), .bit_10(reg_15[10]), .bit_11(reg_15[11]), .bit_12(reg_15[12]), .bit_13(reg_15[13]),
    .bit_14(reg_15[14]), .bit_15(reg_15[15]), .bit_16(reg_15[16]), .bit_17(reg_15[17]), .bit_18(reg_15[18]),
    .bit_19(reg_15[19]), .bit_20(reg_15[20]), .bit_21(reg_15[21]), .bit_22(reg_15[22]), .bit_23(reg_15[23]),
    .bit_24(reg_15[24]), .bit_25(reg_15[25]), .bit_26(reg_15[26]), .bit_27(reg_15[27]), .bit_28(reg_15[28]),
    .bit_29(reg_15[29]), .bit_30(reg_15[30]), .bit_31(reg_15[31]));
  Registrador_32bits registrador_32bits_21 (
    .CLK(CLK), .in_2(reg_x19), .bit_0(reg_19[0]), .bit_1(reg_19[1]), .bit_2(reg_19[2]), .bit_3(reg_19[3]),
    .bit_4(reg_19[4]), .bit_5(reg_19[5]), .bit_6(reg_19[6]), .bit_7(reg_19[7]), .bit_8(reg_19[8]),
    .bit_9(reg_19[9]), .bit_10(reg_19[10]), .bit_11(reg_19[11]), .bit_12(reg_19[12]), .bit_13(reg_19[13]),
    .bit_14(reg_19[14]), .bit_15(reg_19[15]), .bit_16(reg_19[16]), .bit_17(reg_19[17]), .bit_18(reg_19[18]),
    .bit_19(reg_19[19]), .bit_20(reg_19[20]), .bit_21(reg_19[21]), .bit_22(reg_19[22]), .bit_23(reg_19[23]),
    .bit_24(reg_19[24]), .bit_25(reg_19[25]), .bit_26(reg_19[26]), .bit_27(reg_19[27]), .bit_28(reg_19[28]),
    .bit_29(reg_19[29]), .bit_30(reg_19[30]), .bit_31(reg_19[31]));
  Registrador_32bits registrador_32bits_22 (
    .CLK(CLK), .in_2(reg_x23), .bit_0(reg_23[0]), .bit_1(reg_23[1]), .bit_2(reg_23[2]), .bit_3(reg_23[3]),
    .bit_4(reg_23[4]), .bit_5(reg_23[5]), .bit_6(reg_23[6]), .bit_7(reg_23[7]), .bit_8(reg_23[8]),
    .bit_9(reg_23[9]), .bit_10(reg_23[10]), .bit_11(reg_23[11]), .bit_12(reg_23[12]), .bit_13(reg_23[13]),
    .bit_14(reg_23[14]), .bit_15(reg_23[15]), .bit_16(reg_23[16]), .bit_17(reg_23[17]), .bit_18(reg_23[18]),
    .bit_19(reg_23[19]), .bit_20(reg_23[20]), .bit_21(reg_23[21]), .bit_22(reg_23[22]), .bit_23(reg_23[23]),
    .bit_24(reg_23[24]), .bit_25(reg_23[25]), .bit_26(reg_23[26]), .bit_27(reg_23[27]), .bit_28(reg_23[28]),
    .bit_29(reg_23[29]), .bit_30(reg_23[30]), .bit_31(reg_23[31]));
  Registrador_32bits registrador_32bits_23 (
    .CLK(CLK), .in_2(reg_x27), .bit_0(reg_27[0]), .bit_1(reg_27[1]), .bit_2(reg_27[2]), .bit_3(reg_27[3]),
    .bit_4(reg_27[4]), .bit_5(reg_27[5]), .bit_6(reg_27[6]), .bit_7(reg_27[7]), .bit_8(reg_27[8]),
    .bit_9(reg_27[9]), .bit_10(reg_27[10]), .bit_11(reg_27[11]), .bit_12(reg_27[12]), .bit_13(reg_27[13]),
    .bit_14(reg_27[14]), .bit_15(reg_27[15]), .bit_16(reg_27[16]), .bit_17(reg_27[17]), .bit_18(reg_27[18]),
    .bit_19(reg_27[19]), .bit_20(reg_27[20]), .bit_21(reg_27[21]), .bit_22(reg_27[22]), .bit_23(reg_27[23]),
    .bit_24(reg_27[24]), .bit_25(reg_27[25]), .bit_26(reg_27[26]), .bit_27(reg_27[27]), .bit_28(reg_27[28]),
    .bit_29(reg_27[29]), .bit_30(reg_27[30]), .bit_31(reg_27[31]));
  Registrador_32bits registrador_32bits_24 (
    .CLK(CLK), .in_2(reg_x31), .bit_0(reg_31[0]), .bit_1(reg_31[1]), .bit_2(reg_31[2]), .bit_3(reg_31[3]),
    .bit_4(reg_31[4]), .bit_5(reg_31[5]), .bit_6(reg_31[6]), .bit_7(reg_31[7]), .bit_8(reg_31[8]),
    .bit_9(reg_31[9]), .bit_10(reg_31[10]), .bit_11(reg_31[11]), .bit_12(reg_31[12]), .bit_13(reg_31[13]),
    .bit_14(reg_31[14]), .bit_15(reg_31[15]), .bit_16(reg_31[16]), .bit_17(reg_31[17]), .bit_18(reg_31[18]),
    .bit_19(reg_31[19]), .bit_20(reg_31[20]), .bit_21(reg_31[21]), .bit_22(reg_31[22]), .bit_23(reg_31[23]),
    .bit_24(reg_31[24]), .bit_25(reg_31[25]), .bit_26(reg_31[26]), .bit_27(reg_31[27]), .bit_28(reg_31[28]),
    .bit_29(reg_31[29]), .bit_30(reg_31[30]), .bit_31(reg_31[31]));
  Registrador_32bits registrador_32bits_25 (
    .CLK(CLK), .in_2(reg_x4), .bit_0(reg_4[0]), .bit_1(reg_4[1]), .bit_2(reg_4[2]), .bit_3(reg_4[3]),
    .bit_4(reg_4[4]), .bit_5(reg_4[5]), .bit_6(reg_4[6]), .bit_7(reg_4[7]), .bit_8(reg_4[8]),
    .bit_9(reg_4[9]), .bit_10(reg_4[10]), .bit_11(reg_4[11]), .bit_12(reg_4[12]), .bit_13(reg_4[13]),
    .bit_14(reg_4[14]), .bit_15(reg_4[15]), .bit_16(reg_4[16]), .bit_17(reg_4[17]), .bit_18(reg_4[18]),
    .bit_19(reg_4[19]), .bit_20(reg_4[20]), .bit_21(reg_4[21]), .bit_22(reg_4[22]), .bit_23(reg_4[23]),
    .bit_24(reg_4[24]), .bit_25(reg_4[25]), .bit_26(reg_4[26]), .bit_27(reg_4[27]), .bit_28(reg_4[28]),
    .bit_29(reg_4[29]), .bit_30(reg_4[30]), .bit_31(reg_4[31]));
  Registrador_32bits registrador_32bits_26 (
    .CLK(CLK), .in_2(reg_x8), .bit_0(reg_8[0]), .bit_1(reg_8[1]), .bit_2(reg_8[2]), .bit_3(reg_8[3]),
    .bit_4(reg_8[4]), .bit_5(reg_8[5]), .bit_6(reg_8[6]), .bit_7(reg_8[7]), .bit_8(reg_8[8]),
    .bit_9(reg_8[9]), .bit_10(reg_8[10]), .bit_11(reg_8[11]), .bit_12(reg_8[12]), .bit_13(reg_8[13]),
    .bit_14(reg_8[14]), .bit_15(reg_8[15]), .bit_16(reg_8[16]), .bit_17(reg_8[17]), .bit_18(reg_8[18]),
    .bit_19(reg_8[19]), .bit_20(reg_8[20]), .bit_21(reg_8[21]), .bit_22(reg_8[22]), .bit_23(reg_8[23]),
    .bit_24(reg_8[24]), .bit_25(reg_8[25]), .bit_26(reg_8[26]), .bit_27(reg_8[27]), .bit_28(reg_8[28]),
    .bit_29(reg_8[29]), .bit_30(reg_8[30]), .bit_31(reg_8[31]));
  Registrador_32bits registrador_32bits_27 (
    .CLK(CLK), .in_2(reg_x12), .bit_0(reg_12[0]), .bit_1(reg_12[1]), .bit_2(reg_12[2]), .bit_3(reg_12[3]),
    .bit_4(reg_12[4]), .bit_5(reg_12[5]), .bit_6(reg_12[6]), .bit_7(reg_12[7]), .bit_8(reg_12[8]),
    .bit_9(reg_12[9]), .bit_10(reg_12[10]), .bit_11(reg_12[11]), .bit_12(reg_12[12]), .bit_13(reg_12[13]),
    .bit_14(reg_12[14]), .bit_15(reg_12[15]), .bit_16(reg_12[16]), .bit_17(reg_12[17]), .bit_18(reg_12[18]),
    .bit_19(reg_12[19]), .bit_20(reg_12[20]), .bit_21(reg_12[21]), .bit_22(reg_12[22]), .bit_23(reg_12[23]),
    .bit_24(reg_12[24]), .bit_25(reg_12[25]), .bit_26(reg_12[26]), .bit_27(reg_12[27]), .bit_28(reg_12[28]),
    .bit_29(reg_12[29]), .bit_30(reg_12[30]), .bit_31(reg_12[31]));
  Registrador_32bits registrador_32bits_28 (
    .CLK(CLK), .in_2(reg_x16), .bit_0(reg_16[0]), .bit_1(reg_16[1]), .bit_2(reg_16[2]), .bit_3(reg_16[3]),
    .bit_4(reg_16[4]), .bit_5(reg_16[5]), .bit_6(reg_16[6]), .bit_7(reg_16[7]), .bit_8(reg_16[8]),
    .bit_9(reg_16[9]), .bit_10(reg_16[10]), .bit_11(reg_16[11]), .bit_12(reg_16[12]), .bit_13(reg_16[13]),
    .bit_14(reg_16[14]), .bit_15(reg_16[15]), .bit_16(reg_16[16]), .bit_17(reg_16[17]), .bit_18(reg_16[18]),
    .bit_19(reg_16[19]), .bit_20(reg_16[20]), .bit_21(reg_16[21]), .bit_22(reg_16[22]), .bit_23(reg_16[23]),
    .bit_24(reg_16[24]), .bit_25(reg_16[25]), .bit_26(reg_16[26]), .bit_27(reg_16[27]), .bit_28(reg_16[28]),
    .bit_29(reg_16[29]), .bit_30(reg_16[30]), .bit_31(reg_16[31]));
  Registrador_32bits registrador_32bits_29 (
    .CLK(CLK), .in_2(reg_x20), .bit_0(reg_20[0]), .bit_1(reg_20[1]), .bit_2(reg_20[2]), .bit_3(reg_20[3]),
    .bit_4(reg_20[4]), .bit_5(reg_20[5]), .bit_6(reg_20[6]), .bit_7(reg_20[7]), .bit_8(reg_20[8]),
    .bit_9(reg_20[9]), .bit_10(reg_20[10]), .bit_11(reg_20[11]), .bit_12(reg_20[12]), .bit_13(reg_20[13]),
    .bit_14(reg_20[14]), .bit_15(reg_20[15]), .bit_16(reg_20[16]), .bit_17(reg_20[17]), .bit_18(reg_20[18]),
    .bit_19(reg_20[19]), .bit_20(reg_20[20]), .bit_21(reg_20[21]), .bit_22(reg_20[22]), .bit_23(reg_20[23]),
    .bit_24(reg_20[24]), .bit_25(reg_20[25]), .bit_26(reg_20[26]), .bit_27(reg_20[27]), .bit_28(reg_20[28]),
    .bit_29(reg_20[29]), .bit_30(reg_20[30]), .bit_31(reg_20[31]));
  Registrador_32bits registrador_32bits_30 (
    .CLK(CLK), .in_2(reg_x24), .bit_0(reg_24[0]), .bit_1(reg_24[1]), .bit_2(reg_24[2]), .bit_3(reg_24[3]),
    .bit_4(reg_24[4]), .bit_5(reg_24[5]), .bit_6(reg_24[6]), .bit_7(reg_24[7]), .bit_8(reg_24[8]),
    .bit_9(reg_24[9]), .bit_10(reg_24[10]), .bit_11(reg_24[11]), .bit_12(reg_24[12]), .bit_13(reg_24[13]),
    .bit_14(reg_24[14]), .bit_15(reg_24[15]), .bit_16(reg_24[16]), .bit_17(reg_24[17]), .bit_18(reg_24[18]),
    .bit_19(reg_24[19]), .bit_20(reg_24[20]), .bit_21(reg_24[21]), .bit_22(reg_24[22]), .bit_23(reg_24[23]),
    .bit_24(reg_24[24]), .bit_25(reg_24[25]), .bit_26(reg_24[26]), .bit_27(reg_24[27]), .bit_28(reg_24[28]),
    .bit_29(reg_24[29]), .bit_30(reg_24[30]), .bit_31(reg_24[31]));
  Registrador_32bits registrador_32bits_31 (
    .CLK(CLK), .in_2(reg_x28), .bit_0(reg_28[0]), .bit_1(reg_28[1]), .bit_2(reg_28[2]), .bit_3(reg_28[3]),
    .bit_4(reg_28[4]), .bit_5(reg_28[5]), .bit_6(reg_28[6]), .bit_7(reg_28[7]), .bit_8(reg_28[8]),
    .bit_9(reg_28[9]), .bit_10(reg_28[10]), .bit_11(reg_28[11]), .bit_12(reg_28[12]), .bit_13(reg_28[13]),
    .bit_14(reg_28[14]), .bit_15(reg_28[15]), .bit_16(reg_28[16]), .bit_17(reg_28[17]), .bit_18(reg_28[18]),
    .bit_19(reg_28[19]), .bit_20(reg_28[20]), .bit_21(reg_28[21]), .bit_22(reg_28[22]), .bit_23(reg_28[23]),
    .bit_24(reg_28[24]), .bit_25(reg_28[25]), .bit_26(reg_28[26]), .bit_27(reg_28[27]), .bit_28(reg_28[28]),
    .bit_29(reg_28[29]), .bit_30(reg_28[30]), .bit_31(reg_28[31]));
  // also tied to GND on the sheet: {reg_x0[0], reg_x0[1], reg_x0[2], reg_x0[3], reg_x0[4], reg_x0[5], reg_x0[6], reg_x0[7], reg_x0[8], reg_x0[9], reg_x0[10], reg_x0[11], reg_x0[12], reg_x0[13], reg_x0[14], reg_x0[15], reg_x0[16], reg_x0[17], reg_x0[18], reg_x0[19], reg_x0[20], reg_x0[21], reg_x0[22], reg_x0[23], reg_x0[24], reg_x0[25], reg_x0[26], reg_x0[27], reg_x0[28], reg_x0[29], reg_x0[30], reg_x0[31]}
endmodule

module Instruction_Memory (
  input  [7:0] ReadAdress,
  output [31:0] Instruction
);

  wire [7:0] shifter_1_out;

  Shifter #(.shift("lr")) shifter_1 (.in(ReadAdress), .\dist (3'b010), .out(shifter_1_out));
  ROM #(.dataWidth(32)) rom_1 (.addr(shifter_1_out), .data(Instruction));

  // Notes on the sheet:
  //   contents of rom_1 (hex, n*v repeats v):
  //   2083 102103 202183 302203 3102b3 40418333 10f3b3 106433 fe1080e3
endmodule

module PC (
  input  CLK,
  input  [31:0] in_2,
  output [31:0] out_3
);

  Registrador_32bits registrador_32bits_1 (
    .CLK(CLK), .in_2(in_2), .bit_0(out_3[0]), .bit_1(out_3[1]), .bit_2(out_3[2]), .bit_3(out_3[3]),
    .bit_4(out_3[4]), .bit_5(out_3[5]), .bit_6(out_3[6]), .bit_7(out_3[7]), .bit_8(out_3[8]),
    .bit_9(out_3[9]), .bit_10(out_3[10]), .bit_11(out_3[11]), .bit_12(out_3[12]), .bit_13(out_3[13]),
    .bit_14(out_3[14]), .bit_15(out_3[15]), .bit_16(out_3[16]), .bit_17(out_3[17]), .bit_18(out_3[18]),
    .bit_19(out_3[19]), .bit_20(out_3[20]), .bit_21(out_3[21]), .bit_22(out_3[22]), .bit_23(out_3[23]),
    .bit_24(out_3[24]), .bit_25(out_3[25]), .bit_26(out_3[26]), .bit_27(out_3[27]), .bit_28(out_3[28]),
    .bit_29(out_3[29]), .bit_30(out_3[30]), .bit_31(out_3[31]));
endmodule

module Data_Memory (
  input  [7:0] Adress,
  input  MemWrite,
  input  MemRead,
  input  CLK,
  input  [31:0] WriteData,
  output [31:0] ReadData
);

  RAM #(.dataWidth(32)) ram_1 (.addr(Adress), .we(MemWrite), .oe(MemRead), .clk(CLK), .din(WriteData), .dout(ReadData));
endmodule

module ALU (
  input  [31:0] in_1,
  input  [31:0] in_2,
  input  [3:0] ALUOp,
  output Zero,
  output [31:0] out_5
);

  wire not_1_out, not_2_out, not_3_out, not_4_out, not_5_out, not_6_out, not_7_out, not_8_out, not_9_out,
       not_10_out, not_11_out, not_12_out, not_13_out, not_14_out, not_15_out, not_16_out, not_17_out,
       not_18_out, not_19_out, not_20_out, not_21_out, not_22_out, not_23_out, not_24_out, not_25_out,
       not_26_out, not_27_out, not_28_out, not_29_out, not_30_out, not_31_out, not_32_out;
  wire [31:0] adder_1_out, and_1_out, or_1_out, shifter_1_out, subtractor_1_out;

  assign and_1_out = in_1 & in_2;  // AND_Gate and_1, 32 bits wide
  assign or_1_out = in_1 | in_2;  // OR_Gate or_1, 32 bits wide
  Adder #(.width(32)) adder_1 (.a(in_1), .b(in_2), .out(adder_1_out));  // open: cin, cout
  Subtractor #(.width(32)) subtractor_1 (.a(in_1), .b(in_2), .out(subtractor_1_out));  // open: bin, bout
  Shifter #(.width(32)) shifter_1 (.in(in_1), .\dist (in_2[4:0]), .out(shifter_1_out));
  not not_1 (not_1_out, subtractor_1_out[0]);
  not not_2 (not_2_out, subtractor_1_out[1]);
  not not_3 (not_3_out, subtractor_1_out[2]);
  not not_4 (not_4_out, subtractor_1_out[3]);
  not not_5 (not_5_out, subtractor_1_out[4]);
  not not_6 (not_6_out, subtractor_1_out[5]);
  not not_7 (not_7_out, subtractor_1_out[6]);
  not not_8 (not_8_out, subtractor_1_out[7]);
  not not_9 (not_9_out, subtractor_1_out[8]);
  not not_10 (not_10_out, subtractor_1_out[9]);
  not not_11 (not_11_out, subtractor_1_out[10]);
  not not_12 (not_12_out, subtractor_1_out[11]);
  not not_13 (not_13_out, subtractor_1_out[12]);
  not not_14 (not_14_out, subtractor_1_out[13]);
  not not_15 (not_15_out, subtractor_1_out[14]);
  not not_16 (not_16_out, subtractor_1_out[15]);
  not not_17 (not_17_out, subtractor_1_out[16]);
  not not_18 (not_18_out, subtractor_1_out[17]);
  not not_19 (not_19_out, subtractor_1_out[18]);
  not not_20 (not_20_out, subtractor_1_out[19]);
  not not_21 (not_21_out, subtractor_1_out[20]);
  not not_22 (not_22_out, subtractor_1_out[21]);
  not not_23 (not_23_out, subtractor_1_out[22]);
  not not_24 (not_24_out, subtractor_1_out[23]);
  not not_25 (not_25_out, subtractor_1_out[24]);
  not not_26 (not_26_out, subtractor_1_out[25]);
  not not_27 (not_27_out, subtractor_1_out[26]);
  not not_28 (not_28_out, subtractor_1_out[27]);
  not not_29 (not_29_out, subtractor_1_out[28]);
  not not_30 (not_30_out, subtractor_1_out[29]);
  not not_31 (not_31_out, subtractor_1_out[30]);
  not not_32 (not_32_out, subtractor_1_out[31]);
  Multiplexer #(.select(4), .width(32)) multiplexer_1 (
    .in0(and_1_out), .in1(or_1_out), .in2(adder_1_out), .in6(subtractor_1_out), .in7(shifter_1_out),
    .out(out_5), .sel(ALUOp));  // open: in3, in4, in5, in8, in9, in10, in11, in12, in13, in14, in15
  and and_2 (Zero, not_1_out, not_2_out, not_3_out, not_4_out, not_5_out, not_6_out, not_7_out, not_8_out, not_9_out, not_10_out, not_11_out, not_12_out, not_13_out, not_14_out, not_15_out, not_16_out, not_17_out, not_18_out, not_19_out, not_20_out, not_21_out, not_22_out, not_23_out, not_24_out, not_25_out, not_26_out, not_27_out, not_28_out, not_29_out, not_30_out, not_31_out, not_32_out);
endmodule

module ImmGen (
  input  [31:0] in_1,
  output [31:0] S1
);

  wire [31:0] B, I, S;

  // Probe on {in_1[31:25], in_1[11:7]}
  assign S = {{20{in_1[31]}}, {in_1[31:25], in_1[11:7]}};  // Bit_Extender bit_extender_1
  assign I = {{20{in_1[31]}}, in_1[31:20]};  // Bit_Extender bit_extender_2
  // Probe on in_1[31:20]
  assign B = {{19{in_1[31]}}, {in_1[31], in_1[7], in_1[30:25], in_1[11:8], 1'b0}};  // Bit_Extender bit_extender_3
  // Probe on {in_1[31], in_1[7], in_1[30:25], in_1[11:8], 1'b0}
  Multiplexer #(.select(2), .width(32)) multiplexer_1 (
    .in0(I), .in1(S), .in3(B), .out(S1), .sel(in_1[6:5]));  // open: in2

  // Other names for the same wires on the sheet: opcode[1:0] = in_1[6:5]
endmodule

module Control (
  input  [6:0] opcode,
  input  [1:0] funct3,
  output AluSrc,
  output MemToReg,
  output RegWrite,
  output MemRead,
  output MemWrite,
  output Branch,
  output AluOp0,
  output AluOp1
);

  wire and_1_out, and_2_out, and_3_out, and_4_out, and_6_out, and_7_out, and_10_out, and_11_out;

  and and_1 (and_1_out, ~opcode[6], ~opcode[5], ~opcode[4], ~funct3[1], funct3[0]);  // AND_Gate
  and and_2 (and_2_out, ~opcode[6], ~opcode[5], ~opcode[4], ~funct3[1], funct3[0]);  // AND_Gate
  and and_3 (and_3_out, ~opcode[6], opcode[5], ~opcode[4]);  // AND_Gate
  and and_4 (and_4_out, ~opcode[6], ~opcode[5], ~opcode[5]);  // AND_Gate
  and and_5 (MemRead, ~opcode[6], ~opcode[5], ~opcode[4], funct3[1], ~funct3[0]);  // AND_Gate
  and and_6 (and_6_out, ~opcode[6], opcode[5], opcode[4]);  // AND_Gate
  and and_7 (and_7_out, ~opcode[6], ~opcode[5], ~opcode[4]);  // AND_Gate
  and and_8 (MemWrite, ~opcode[6], opcode[5], ~opcode[4]);  // AND_Gate
  and and_9 (Branch, opcode[6], opcode[5], ~opcode[4]);  // AND_Gate
  and and_10 (and_10_out, opcode[6], opcode[5], ~opcode[4]);  // AND_Gate
  and and_11 (and_11_out, ~opcode[6], opcode[5], opcode[4]);  // AND_Gate
  or or_1 (AluSrc, and_3_out, and_4_out);
  or or_2 (RegWrite, and_6_out, and_7_out);
  or or_3 (AluOp0, and_10_out, and_1_out);
  or or_4 (AluOp1, and_2_out, and_11_out);

  assign MemToReg = MemRead;

  // Other names for the same wires on the sheet: f0 = funct3[0]; f1 = funct3[1]; op4 = opcode[4]; op5 = opcode[5];
  //   op6 = opcode[6]
endmodule

module ALU_Control (
  input  [5:0] in_1,
  input  [5:0] in_2,
  output [3:0] out_3,
  output [3:0] out_4
);

  wire add_out, and_1_out, and_2_out, and_3_out, and_4_out, and_5_out, beq1_out, beq_out, lwEsw_out,
       not_1_out, not_2_out, not_3_out, or_1_out;

  and and_1 (and_1_out, in_1[5], ~in_1[4], ~in_1[3], in_1[2], in_1[1], ~in_1[0]);  // AND_Gate
  and and_2 (and_2_out, in_1[5], in_1[4]);
  and and_3 (and_3_out, ~in_1[0], ~in_1[1], ~in_1[2], in_1[3], ~in_1[4], in_1[5]);  // AND_Gate
  and and_4 (and_4_out, in_1[4], ~in_1[5]);  // AND_Gate
  and and_5 (and_5_out, in_1[4], in_1[5]);
  or or_1 (or_1_out, and_3_out, and_4_out);
  or or_2 (out_4[0], and_1_out, and_2_out);
  or or_3 (out_4[2], or_1_out, and_5_out);
  not not_1 (not_1_out, in_2[3]);
  not not_2 (not_2_out, in_2[0]);
  not not_3 (not_3_out, in_2[4]);
  and b0 (out_3[0], not_2_out, in_2[1], in_2[2], not_1_out, not_3_out, in_2[5]);
  and lwEsw (lwEsw_out, ~in_2[4], ~in_2[5]);  // AND_Gate
  and beq (beq_out, in_2[4], ~in_2[5]);  // AND_Gate
  and add (add_out, in_2[5], ~in_2[4], ~in_2[3], ~in_2[2], ~in_2[1], ~in_2[0]);  // AND_Gate
  and beq1 (beq1_out, in_2[4], ~in_2[5]);  // AND_Gate
  or b1 (out_3[1], lwEsw_out, beq_out, add_out, in_2[3]);
  or b2 (out_3[2], beq1_out, in_2[3]);

  assign out_3[3] = 1'b0;
  assign out_4[3] = 1'b0;

  // Other names for the same wires on the sheet: bit12 = in_1[0]; bit13 = in_1[1]; bit14 = in_1[2]; bit30 = in_1[3];
  //   ALUop0 = in_1[4]; ALUop1 = in_1[5]
endmodule

module IFtoID (
  input  CLK,
  input  [31:0] PCin,
  input  [31:0] INSTin,
  output [31:0] PCout,
  output [31:0] INSTout
);

  Registrador_32bits registrador_32bits_1 (
    .CLK(CLK), .in_2(PCin), .bit_0(PCout[0]), .bit_1(PCout[1]), .bit_2(PCout[2]), .bit_3(PCout[3]),
    .bit_4(PCout[4]), .bit_5(PCout[5]), .bit_6(PCout[6]), .bit_7(PCout[7]), .bit_8(PCout[8]),
    .bit_9(PCout[9]), .bit_10(PCout[10]), .bit_11(PCout[11]), .bit_12(PCout[12]), .bit_13(PCout[13]),
    .bit_14(PCout[14]), .bit_15(PCout[15]), .bit_16(PCout[16]), .bit_17(PCout[17]), .bit_18(PCout[18]),
    .bit_19(PCout[19]), .bit_20(PCout[20]), .bit_21(PCout[21]), .bit_22(PCout[22]), .bit_23(PCout[23]),
    .bit_24(PCout[24]), .bit_25(PCout[25]), .bit_26(PCout[26]), .bit_27(PCout[27]), .bit_28(PCout[28]),
    .bit_29(PCout[29]), .bit_30(PCout[30]), .bit_31(PCout[31]));
  Registrador_32bits registrador_32bits_2 (
    .CLK(CLK), .in_2(INSTin), .bit_0(INSTout[0]), .bit_1(INSTout[1]), .bit_2(INSTout[2]), .bit_3(INSTout[3]),
    .bit_4(INSTout[4]), .bit_5(INSTout[5]), .bit_6(INSTout[6]), .bit_7(INSTout[7]), .bit_8(INSTout[8]),
    .bit_9(INSTout[9]), .bit_10(INSTout[10]), .bit_11(INSTout[11]), .bit_12(INSTout[12]),
    .bit_13(INSTout[13]), .bit_14(INSTout[14]), .bit_15(INSTout[15]), .bit_16(INSTout[16]),
    .bit_17(INSTout[17]), .bit_18(INSTout[18]), .bit_19(INSTout[19]), .bit_20(INSTout[20]),
    .bit_21(INSTout[21]), .bit_22(INSTout[22]), .bit_23(INSTout[23]), .bit_24(INSTout[24]),
    .bit_25(INSTout[25]), .bit_26(INSTout[26]), .bit_27(INSTout[27]), .bit_28(INSTout[28]),
    .bit_29(INSTout[29]), .bit_30(INSTout[30]), .bit_31(INSTout[31]));
endmodule

module IDtoEX (
  input  CLK,
  input  ALUSRCin,
  input  MEMTOREGin,
  input  REGWRITEin,
  input  MEMREADin,
  input  MEMWRITEin,
  input  BRANCHin,
  input  ALUOP0in,
  input  ALUOP1in,
  input  [31:0] PCin,
  input  [31:0] RD1in,
  input  [31:0] RD2in,
  input  [31:0] IMMin,
  input  [4:0] WRITERGin,
  output ALUSRCout,
  output MEMTOREGout,
  output REGWRITEout,
  output MEMREADout,
  output MEMWRITEout,
  output BRANCHout,
  output ALUOP0out,
  output ALUOP1out,
  output [31:0] PCout,
  output [31:0] RD1out,
  output [31:0] RD2out,
  output [31:0] IMMout,
  output [4:0] WRITERGout
);

  D_Flip_Flop d_ff_1 (.D(ALUSRCin), .clk(CLK), .Q(ALUSRCout));  // open: Qn, preset, reset
  D_Flip_Flop d_ff_2 (.D(MEMTOREGin), .clk(CLK), .Q(MEMTOREGout));  // open: Qn, preset, reset
  D_Flip_Flop d_ff_3 (.D(REGWRITEin), .clk(CLK), .Q(REGWRITEout));  // open: Qn, preset, reset
  D_Flip_Flop d_ff_4 (.D(MEMREADin), .clk(CLK), .Q(MEMREADout));  // open: Qn, preset, reset
  D_Flip_Flop d_ff_5 (.D(MEMWRITEin), .clk(CLK), .Q(MEMWRITEout));  // open: Qn, preset, reset
  D_Flip_Flop d_ff_6 (.D(BRANCHin), .clk(CLK), .Q(BRANCHout));  // open: Qn, preset, reset
  D_Flip_Flop d_ff_7 (.D(ALUOP0in), .clk(CLK), .Q(ALUOP0out));  // open: Qn, preset, reset
  D_Flip_Flop d_ff_8 (.D(ALUOP1in), .clk(CLK), .Q(ALUOP1out));  // open: Qn, preset, reset
  Registrador_32bits registrador_32bits_1 (
    .CLK(CLK), .in_2(IMMin), .bit_0(IMMout[0]), .bit_1(IMMout[1]), .bit_2(IMMout[2]), .bit_3(IMMout[3]),
    .bit_4(IMMout[4]), .bit_5(IMMout[5]), .bit_6(IMMout[6]), .bit_7(IMMout[7]), .bit_8(IMMout[8]),
    .bit_9(IMMout[9]), .bit_10(IMMout[10]), .bit_11(IMMout[11]), .bit_12(IMMout[12]), .bit_13(IMMout[13]),
    .bit_14(IMMout[14]), .bit_15(IMMout[15]), .bit_16(IMMout[16]), .bit_17(IMMout[17]), .bit_18(IMMout[18]),
    .bit_19(IMMout[19]), .bit_20(IMMout[20]), .bit_21(IMMout[21]), .bit_22(IMMout[22]), .bit_23(IMMout[23]),
    .bit_24(IMMout[24]), .bit_25(IMMout[25]), .bit_26(IMMout[26]), .bit_27(IMMout[27]), .bit_28(IMMout[28]),
    .bit_29(IMMout[29]), .bit_30(IMMout[30]), .bit_31(IMMout[31]));
  Registrador_5bits registrador_5bits_1 (
    .CLK(CLK), .in_2(WRITERGin), .bit_0(WRITERGout[0]), .bit_1(WRITERGout[1]), .bit_2(WRITERGout[2]),
    .bit_3(WRITERGout[3]), .bit_4(WRITERGout[4]));
  Registrador_32bits registrador_32bits_2 (
    .CLK(CLK), .in_2(PCin), .bit_0(PCout[0]), .bit_1(PCout[1]), .bit_2(PCout[2]), .bit_3(PCout[3]),
    .bit_4(PCout[4]), .bit_5(PCout[5]), .bit_6(PCout[6]), .bit_7(PCout[7]), .bit_8(PCout[8]),
    .bit_9(PCout[9]), .bit_10(PCout[10]), .bit_11(PCout[11]), .bit_12(PCout[12]), .bit_13(PCout[13]),
    .bit_14(PCout[14]), .bit_15(PCout[15]), .bit_16(PCout[16]), .bit_17(PCout[17]), .bit_18(PCout[18]),
    .bit_19(PCout[19]), .bit_20(PCout[20]), .bit_21(PCout[21]), .bit_22(PCout[22]), .bit_23(PCout[23]),
    .bit_24(PCout[24]), .bit_25(PCout[25]), .bit_26(PCout[26]), .bit_27(PCout[27]), .bit_28(PCout[28]),
    .bit_29(PCout[29]), .bit_30(PCout[30]), .bit_31(PCout[31]));
  Registrador_32bits registrador_32bits_3 (
    .CLK(CLK), .in_2(RD1in), .bit_0(RD1out[0]), .bit_1(RD1out[1]), .bit_2(RD1out[2]), .bit_3(RD1out[3]),
    .bit_4(RD1out[4]), .bit_5(RD1out[5]), .bit_6(RD1out[6]), .bit_7(RD1out[7]), .bit_8(RD1out[8]),
    .bit_9(RD1out[9]), .bit_10(RD1out[10]), .bit_11(RD1out[11]), .bit_12(RD1out[12]), .bit_13(RD1out[13]),
    .bit_14(RD1out[14]), .bit_15(RD1out[15]), .bit_16(RD1out[16]), .bit_17(RD1out[17]), .bit_18(RD1out[18]),
    .bit_19(RD1out[19]), .bit_20(RD1out[20]), .bit_21(RD1out[21]), .bit_22(RD1out[22]), .bit_23(RD1out[23]),
    .bit_24(RD1out[24]), .bit_25(RD1out[25]), .bit_26(RD1out[26]), .bit_27(RD1out[27]), .bit_28(RD1out[28]),
    .bit_29(RD1out[29]), .bit_30(RD1out[30]), .bit_31(RD1out[31]));
  Registrador_32bits registrador_32bits_4 (
    .CLK(CLK), .in_2(RD2in), .bit_0(RD2out[0]), .bit_1(RD2out[1]), .bit_2(RD2out[2]), .bit_3(RD2out[3]),
    .bit_4(RD2out[4]), .bit_5(RD2out[5]), .bit_6(RD2out[6]), .bit_7(RD2out[7]), .bit_8(RD2out[8]),
    .bit_9(RD2out[9]), .bit_10(RD2out[10]), .bit_11(RD2out[11]), .bit_12(RD2out[12]), .bit_13(RD2out[13]),
    .bit_14(RD2out[14]), .bit_15(RD2out[15]), .bit_16(RD2out[16]), .bit_17(RD2out[17]), .bit_18(RD2out[18]),
    .bit_19(RD2out[19]), .bit_20(RD2out[20]), .bit_21(RD2out[21]), .bit_22(RD2out[22]), .bit_23(RD2out[23]),
    .bit_24(RD2out[24]), .bit_25(RD2out[25]), .bit_26(RD2out[26]), .bit_27(RD2out[27]), .bit_28(RD2out[28]),
    .bit_29(RD2out[29]), .bit_30(RD2out[30]), .bit_31(RD2out[31]));
endmodule

module EXtoMEM (
  input  CLK,
  input  MEMTOREGin,
  input  REGWRITEin,
  input  MEMREADin,
  input  MEMWRITEin,
  input  BRANCHin,
  input  [31:0] PCin,
  input  ZEROin,
  input  [31:0] ALUin,
  input  [31:0] RD2in,
  input  [4:0] WRITERGin,
  output MEMTOREGout,
  output REGWRITEout,
  output MEMREADout,
  output MEMWRITEout,
  output BRANCHout,
  output [31:0] PCout,
  output ZEROout,
  output [31:0] ALUout,
  output [31:0] RD2out,
  output [4:0] WRITERGout
);

  D_Flip_Flop d_ff_1 (.D(MEMTOREGin), .clk(CLK), .Q(MEMTOREGout));  // open: Qn, preset, reset
  D_Flip_Flop d_ff_2 (.D(REGWRITEin), .clk(CLK), .Q(REGWRITEout));  // open: Qn, preset, reset
  D_Flip_Flop d_ff_3 (.D(MEMREADin), .clk(CLK), .Q(MEMREADout));  // open: Qn, preset, reset
  D_Flip_Flop d_ff_4 (.D(MEMWRITEin), .clk(CLK), .Q(MEMWRITEout));  // open: Qn, preset, reset
  D_Flip_Flop d_ff_5 (.D(BRANCHin), .clk(CLK), .Q(BRANCHout));  // open: Qn, preset, reset
  D_Flip_Flop d_ff_6 (.D(ZEROin), .clk(CLK), .Q(ZEROout));  // open: Qn, preset, reset
  Registrador_32bits registrador_32bits_1 (
    .CLK(CLK), .in_2(ALUin), .bit_0(ALUout[0]), .bit_1(ALUout[1]), .bit_2(ALUout[2]), .bit_3(ALUout[3]),
    .bit_4(ALUout[4]), .bit_5(ALUout[5]), .bit_6(ALUout[6]), .bit_7(ALUout[7]), .bit_8(ALUout[8]),
    .bit_9(ALUout[9]), .bit_10(ALUout[10]), .bit_11(ALUout[11]), .bit_12(ALUout[12]), .bit_13(ALUout[13]),
    .bit_14(ALUout[14]), .bit_15(ALUout[15]), .bit_16(ALUout[16]), .bit_17(ALUout[17]), .bit_18(ALUout[18]),
    .bit_19(ALUout[19]), .bit_20(ALUout[20]), .bit_21(ALUout[21]), .bit_22(ALUout[22]), .bit_23(ALUout[23]),
    .bit_24(ALUout[24]), .bit_25(ALUout[25]), .bit_26(ALUout[26]), .bit_27(ALUout[27]), .bit_28(ALUout[28]),
    .bit_29(ALUout[29]), .bit_30(ALUout[30]), .bit_31(ALUout[31]));
  Registrador_32bits registrador_32bits_2 (
    .CLK(CLK), .in_2(RD2in), .bit_0(RD2out[0]), .bit_1(RD2out[1]), .bit_2(RD2out[2]), .bit_3(RD2out[3]),
    .bit_4(RD2out[4]), .bit_5(RD2out[5]), .bit_6(RD2out[6]), .bit_7(RD2out[7]), .bit_8(RD2out[8]),
    .bit_9(RD2out[9]), .bit_10(RD2out[10]), .bit_11(RD2out[11]), .bit_12(RD2out[12]), .bit_13(RD2out[13]),
    .bit_14(RD2out[14]), .bit_15(RD2out[15]), .bit_16(RD2out[16]), .bit_17(RD2out[17]), .bit_18(RD2out[18]),
    .bit_19(RD2out[19]), .bit_20(RD2out[20]), .bit_21(RD2out[21]), .bit_22(RD2out[22]), .bit_23(RD2out[23]),
    .bit_24(RD2out[24]), .bit_25(RD2out[25]), .bit_26(RD2out[26]), .bit_27(RD2out[27]), .bit_28(RD2out[28]),
    .bit_29(RD2out[29]), .bit_30(RD2out[30]), .bit_31(RD2out[31]));
  Registrador_5bits registrador_5bits_1 (
    .CLK(CLK), .in_2(WRITERGin), .bit_0(WRITERGout[0]), .bit_1(WRITERGout[1]), .bit_2(WRITERGout[2]),
    .bit_3(WRITERGout[3]), .bit_4(WRITERGout[4]));
  Registrador_32bits registrador_32bits_3 (
    .CLK(CLK), .in_2(PCin), .bit_0(PCout[0]), .bit_1(PCout[1]), .bit_2(PCout[2]), .bit_3(PCout[3]),
    .bit_4(PCout[4]), .bit_5(PCout[5]), .bit_6(PCout[6]), .bit_7(PCout[7]), .bit_8(PCout[8]),
    .bit_9(PCout[9]), .bit_10(PCout[10]), .bit_11(PCout[11]), .bit_12(PCout[12]), .bit_13(PCout[13]),
    .bit_14(PCout[14]), .bit_15(PCout[15]), .bit_16(PCout[16]), .bit_17(PCout[17]), .bit_18(PCout[18]),
    .bit_19(PCout[19]), .bit_20(PCout[20]), .bit_21(PCout[21]), .bit_22(PCout[22]), .bit_23(PCout[23]),
    .bit_24(PCout[24]), .bit_25(PCout[25]), .bit_26(PCout[26]), .bit_27(PCout[27]), .bit_28(PCout[28]),
    .bit_29(PCout[29]), .bit_30(PCout[30]), .bit_31(PCout[31]));
endmodule

module MEMtoWB (
  input  CLK,
  input  MEMTOREGin,
  input  REGWRITEin,
  input  [31:0] RDin,
  input  [31:0] ALUin,
  input  [4:0] WRITERGin,
  output MEMTOREGout,
  output REGWRITEout,
  output [31:0] RDout,
  output [31:0] ALUout,
  output [4:0] WRITERGout
);

  D_Flip_Flop d_ff_1 (.D(MEMTOREGin), .clk(CLK), .Q(MEMTOREGout));  // open: Qn, preset, reset
  D_Flip_Flop d_ff_2 (.D(REGWRITEin), .clk(CLK), .Q(REGWRITEout));  // open: Qn, preset, reset
  Registrador_32bits registrador_32bits_1 (
    .CLK(CLK), .in_2(ALUin), .bit_0(ALUout[0]), .bit_1(ALUout[1]), .bit_2(ALUout[2]), .bit_3(ALUout[3]),
    .bit_4(ALUout[4]), .bit_5(ALUout[5]), .bit_6(ALUout[6]), .bit_7(ALUout[7]), .bit_8(ALUout[8]),
    .bit_9(ALUout[9]), .bit_10(ALUout[10]), .bit_11(ALUout[11]), .bit_12(ALUout[12]), .bit_13(ALUout[13]),
    .bit_14(ALUout[14]), .bit_15(ALUout[15]), .bit_16(ALUout[16]), .bit_17(ALUout[17]), .bit_18(ALUout[18]),
    .bit_19(ALUout[19]), .bit_20(ALUout[20]), .bit_21(ALUout[21]), .bit_22(ALUout[22]), .bit_23(ALUout[23]),
    .bit_24(ALUout[24]), .bit_25(ALUout[25]), .bit_26(ALUout[26]), .bit_27(ALUout[27]), .bit_28(ALUout[28]),
    .bit_29(ALUout[29]), .bit_30(ALUout[30]), .bit_31(ALUout[31]));
  Registrador_5bits registrador_5bits_1 (
    .CLK(CLK), .in_2(WRITERGin), .bit_0(WRITERGout[0]), .bit_1(WRITERGout[1]), .bit_2(WRITERGout[2]),
    .bit_3(WRITERGout[3]), .bit_4(WRITERGout[4]));
  Registrador_32bits registrador_32bits_2 (
    .CLK(CLK), .in_2(RDin), .bit_0(RDout[0]), .bit_1(RDout[1]), .bit_2(RDout[2]), .bit_3(RDout[3]),
    .bit_4(RDout[4]), .bit_5(RDout[5]), .bit_6(RDout[6]), .bit_7(RDout[7]), .bit_8(RDout[8]),
    .bit_9(RDout[9]), .bit_10(RDout[10]), .bit_11(RDout[11]), .bit_12(RDout[12]), .bit_13(RDout[13]),
    .bit_14(RDout[14]), .bit_15(RDout[15]), .bit_16(RDout[16]), .bit_17(RDout[17]), .bit_18(RDout[18]),
    .bit_19(RDout[19]), .bit_20(RDout[20]), .bit_21(RDout[21]), .bit_22(RDout[22]), .bit_23(RDout[23]),
    .bit_24(RDout[24]), .bit_25(RDout[25]), .bit_26(RDout[26]), .bit_27(RDout[27]), .bit_28(RDout[28]),
    .bit_29(RDout[29]), .bit_30(RDout[30]), .bit_31(RDout[31]));
endmodule

module Registrador_5bits (
  input  CLK,
  input  [4:0] in_2,
  output bit_0,
  output bit_1,
  output bit_2,
  output bit_3,
  output bit_4
);

  D_Flip_Flop d_ff_1 (.D(in_2[0]), .clk(CLK), .Q(bit_0));  // open: Qn, preset, reset
  D_Flip_Flop d_ff_2 (.D(in_2[3]), .clk(CLK), .Q(bit_3));  // open: Qn, preset, reset
  D_Flip_Flop d_ff_3 (.D(in_2[1]), .clk(CLK), .Q(bit_1));  // open: Qn, preset, reset
  D_Flip_Flop d_ff_4 (.D(in_2[4]), .clk(CLK), .Q(bit_4));  // open: Qn, preset, reset
  D_Flip_Flop d_ff_5 (.D(in_2[2]), .clk(CLK), .Q(bit_2));  // open: Qn, preset, reset

  // Other names for the same wires on the sheet: bit_0_t = in_2[0]; bit_1_t = in_2[1]; bit_2_t = in_2[2];
  //   bit_3_t = in_2[3]; bit_4_t = in_2[4]
endmodule
